# Fritzing sketch active_buzzer_schematic (saved by Fritzing 0.9.4)
breadboards: 1

parts:
  Arduino = Arduino Mega ADK (Rev3)
  Q1 = TRANSISTOR_NPN [package=to-92-ammo]
  B3 = Piezo Speaker
  B2 = Piezo Speaker
  B1 = Piezo Speaker
  R1 = Resistor [tolerance=±5% resistance=7k package=THT]  # not connected

nets (from the schematic view):
  N1: Arduino.IOREF, Arduino.5V, B3.pin2, B2.pin2, B1.pin2
  N2: Arduino.GND, Q1.E
  N3: Arduino.D2_PWM, Q1.B
  N4: Q1.C, B3.pin1, B2.pin1, B1.pin1
